// Logisim project universalShift.circ as structural Verilog: 1 circuit, main circuit main
module main (
  input  Set,
  input  for_right,
  input  Preset,
  input  D1,
  input  S0,
  input  S1,
  input  D2,
  input  D3,
  input  D4,
  input  in_10,
  output Q1,
  output Q2,
  output Q3,
  output Q4
);

  wire clock_1_out, multiplexer_1_out, multiplexer_2_out, multiplexer_3_out, multiplexer_4_out;

  Multiplexer #(.select(2)) multiplexer_1 (
    .in0(D1), .in1(Q2), .in2(for_right), .in3(Q1), .out(multiplexer_1_out), .sel({S1, S0}));
  Multiplexer #(.select(2)) multiplexer_2 (
    .in0(D2), .in1(Q3), .in2(Q1), .in3(Q2), .out(multiplexer_2_out), .sel({S1, S0}));
  Multiplexer #(.select(2)) multiplexer_3 (
    .in0(D3), .in1(Q4), .in2(Q2), .in3(Q3), .out(multiplexer_3_out), .sel({S1, S0}));
  Multiplexer #(.select(2)) multiplexer_4 (
    .in0(D4), .in1(in_10), .in2(Q3), .in3(Q4), .out(multiplexer_4_out), .sel({S1, S0}));
  Clock clock_1 (.out(clock_1_out));
  D_Flip_Flop d_ff_1 (.D(multiplexer_1_out), .clk(clock_1_out), .Q(Q1), .preset(Set), .reset(Preset));  // open: Qn
  D_Flip_Flop d_ff_2 (.D(multiplexer_2_out), .clk(clock_1_out), .Q(Q2), .preset(Set), .reset(Preset));  // open: Qn
  D_Flip_Flop d_ff_3 (.D(multiplexer_3_out), .clk(clock_1_out), .Q(Q3), .preset(Set), .reset(Preset));  // open: Qn
  D_Flip_Flop d_ff_4 (.D(multiplexer_4_out), .clk(clock_1_out), .Q(Q4), .preset(Set), .reset(Preset));  // open: Qn

  // Notes on the sheet:
  //   for left
endmodule
